# Fritzing sketch arduinoElevatorTrimOLED (saved by Fritzing 0.9.3b)
breadboards: 1

parts:
  C7 = Capacitor Polarized [package=cpol-radial-100uf-25v]
  OLED_I2C1 = OLED 128x64 I2C Monochrome Display
  R1 = Trimmer Potentiometer [maximum_resistance=10kΩ package=THT]
  Componente1 = Arduino Nano (Rev3.0)

nets:
  N1: C7.+, R1.leg2, Componente1.5V
  GND: C7.-, OLED_I2C1.GND, R1.leg1, Componente1.GND
  N2: OLED_I2C1.SDA, Componente1.A4
  N3: OLED_I2C1.SCK, Componente1.A5
  VDD: OLED_I2C1.VDD, Componente1.3V3
  N4: R1.wiper, Componente1.A6
